# Fritzing sketch day3Project2 (saved by Fritzing 0.9.3b)
breadboards: 1

parts:
  Part1 = Arduino Uno (Rev3)
  U1 = POT [package=pot_alpha_rv16af-20]
  R1 = Resistor [tolerance=±5% resistance=220 package=THT]
  LED1 = smd LED [color="Red (633nm)" package="1206 [SMD]"]

nets:
  N1: Part1.A0, U1.S
  N2: Part1.D12/MISO, R1.Pin_0
  N3: Part1.5V, U1.A
  N4: Part1.GND, U1.E, LED1.cathode
  N5: R1.Pin_1, LED1.anode
