# Fritzing sketch single led (saved by Fritzing 0.9.3b)
breadboards: 1

parts:
  Part2 = Arduino Uno (Rev3)
  R1 = Resistor [tolerance=±5% resistance=220 package=THT]
  LED1 = smd LED [color="Red (633nm)" package="0603 [SMD]"]

nets:
  N1: Part2.D12/MISO, LED1.anode
  N2: Part2.GND, R1.Pin_0
  N3: R1.Pin_1, LED1.cathode
