# Fritzing sketch single led3 (saved by Fritzing 0.9.3b)
breadboards: 1

parts:
  Part2 = Arduino Uno (Rev3)
  R1 = Resistor [tolerance=±5% resistance=220 package=THT]
  R2 = Resistor [tolerance=±5% resistance=220 package=THT]
  R3 = Resistor [tolerance=±5% resistance=220 package=THT]
  LED3 = smd LED [color="Green (555nm)" package="0603 [SMD]"]
  LED2 = smd LED [color="Yellow (595nm)" package="0603 [SMD]"]
  LED4 = smd LED [color="Red (633nm)" package="0603 [SMD]"]

nets:
  N1: Part2.D10_PWM/SS, LED3.anode
  N2: Part2.D11_PWM/MOSI, LED2.anode
  N3: Part2.D12/MISO, LED4.anode
  N4: Part2.GND, R1.Pin_0, R2.Pin_0, R3.Pin_0
  N5: R1.Pin_1, LED2.cathode
  N6: R2.Pin_1, LED4.cathode
  N7: R3.Pin_1, LED3.cathode
