# Fritzing sketch single rgb (saved by Fritzing 0.9.3b)
breadboards: 1

parts:
  Part2 = Arduino Uno (Rev3)
  R3 = Resistor [tolerance=±5% resistance=220 package=THT]
  LED5 = RGB LED (com. cathode, rgb) [package="5 mm [THT]"]
  R5 = Resistor [tolerance=±5% resistance=220 package=THT]
  R6 = Resistor [tolerance=±5% resistance=220 package=THT]

nets:
  N1: Part2.D9_PWM, R6.Pin_0
  N2: Part2.D10_PWM/SS, R5.Pin_0
  N3: Part2.D11_PWM/MOSI, R3.Pin_0
  N4: Part2.GND, LED5.common_cathode
  N5: R3.Pin_1, LED5.red_anode
  N6: LED5.green_anode, R5.Pin_1
  N7: LED5.blue_anode, R6.Pin_1
